# Fritzing sketch loom-with-8-servos-5-lights (saved by Fritzing 0.9.3b)
breadboards: 1

parts:
  Part1 = Adafruit Metro with Headers [part_number="Adafruit #2488"]
  Part2 = 16-Channel 12-bit PWM Servo Driver - I2C [part_number=815]
  J1 = Basic Servo
  J14 = Basic Servo
  J15 = Basic Servo
  BATT1 = 4xAA Switchable Battery Pack w/Bare Wire
  J12 = Basic Servo
  R5 = Resistor [tolerance=±5% resistance=220 package=THT]
  R6 = Resistor [tolerance=±5% resistance=220 package=THT]
  R7 = Resistor [tolerance=±5% resistance=220 package=THT]
  R8 = Resistor [tolerance=±5% resistance=220 package=THT]
  LED4 = LED - 5mm [color="Red (633nm)" package="5 mm [THT]"]
  LED5 = LED - 5mm [color="Red (633nm)" package="5 mm [THT]"]
  LED6 = LED - 5mm [color="Red (633nm)" package="5 mm [THT]"]
  R9 = Resistor [tolerance=±5% resistance=220 package=THT]
  LED7 = LED - 5mm [color="Red (633nm)" package="5 mm [THT]"]
  LED8 = LED - 5mm [color="Red (633nm)" package="5 mm [THT]"]
  J13 = Basic Servo
  J16 = Basic Servo
  J17 = Basic Servo
  J18 = Basic Servo

nets:
  N1: Part1.AD5/SCL, Part2.SCL
  N2: Part1.MISO, LED6.anode
  N3: Part1.MOSI, LED4.anode
  N4: Part1.AD4/SDA, Part2.SDA
  GND: Part1.GND, Part2.GND, J1.gnd, J14.gnd, J15.gnd, BATT1.NEG, J12.gnd, J13.gnd, J16.gnd, J17.gnd, J18.gnd
  N5: Part1.SCK, LED5.anode
  N6: Part1.SS, LED7.anode
  N7: Part1.IO9, LED8.anode
  N8: Part1.3.3V, R5.Pin_1, R6.Pin_1, R7.Pin_0, R7.Pin_1, R8.Pin_1, LED6.cathode, R9.Pin_1
  +5V: Part1.+5V, Part2.VCC
  N9: Part2.PWRIN, BATT1.POS
  N10: Part2.PWM7, J17.pulse
  VCC: Part2.5.0V, J1.vcc, J14.vcc, J15.vcc, J12.vcc, J13.vcc, J16.vcc, J17.vcc, J18.vcc
  N11: Part2.PWM6, J16.pulse
  N12: Part2.PWM5, J14.pulse
  N13: Part2.PWM4, J15.pulse
  N14: Part2.PWM3, J13.pulse
  N15: Part2.PWM2, J12.pulse
  N16: Part2.PWM0, J1.pulse
  N17: Part2.PWM8, J18.pulse
  N18: R5.Pin_0, LED4.cathode
  N19: R6.Pin_0, LED7.cathode
  N20: R8.Pin_0, LED5.cathode
  N21: R9.Pin_0, LED8.cathode

custom parts:
  Adafruit Metro with Headers: We sure love the ATmega328 here at Adafruit, and we use them a lot for our own projects. The processor has plenty of GPIO, Analog inputs, hardware UART SPI and I2C, timers and PWM galore - just enough for most simple projects. When we need to go small, we use a Pro Trinket 3V or 5V, but when size isn't as much of a concern, and an USB-serial converter is required, we reach for an Adafruit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
  16-Channel 12-bit PWM Servo Driver - I2C: You want to make a cool robot, maybe a hexapod walker, or maybe just a piece of art with a lot of moving parts. Or maybe you want to drive a lot of LEDs with precise PWM output. Using only two pins, control 16 free-running PWM outputs! You can even chain up 62 breakouts to control up to 992 PWM outputs.
  4xAA Switchable Battery Pack w/Bare Wire: 4xAA Switchable Battery Pack with Bare Wire connection
